// Logisim project decoder.circ as structural Verilog: 1 circuit, main circuit main
module main (
  input  D,
  input  B,
  input  C,
  input  MSB,
  output out_5,
  output out_6,
  output out_7,
  output out_8,
  output D13,
  output out_10,
  output out_11,
  output out_12,
  output out_13,
  output D3,
  output out_15,
  output out_16,
  output out_17,
  output out_18,
  output D9,
  output D15
);

  wire not_1_out, not_2_out, not_3_out, not_4_out;

  and and_1 (out_11, not_1_out, not_2_out, not_3_out, not_4_out);
  not not_1 (not_1_out, MSB);
  and and_2 (out_12, not_1_out, not_2_out, not_3_out, D);
  and and_3 (out_13, not_1_out, not_2_out, C, not_4_out);
  and and_4 (D3, not_1_out, not_2_out, C, D);
  and and_5 (out_15, not_1_out, B, not_3_out, not_4_out);
  not not_2 (not_2_out, B);
  and and_6 (out_16, not_1_out, B, not_3_out, D);
  and and_7 (out_18, not_1_out, B, D, C);
  and and_8 (out_17, not_1_out, B, C, not_4_out);
  and and_9 (out_5, MSB, not_2_out, not_3_out, not_4_out);
  not not_3 (not_3_out, C);
  and and_10 (D9, MSB, not_2_out, not_3_out, D);
  and and_11 (out_6, MSB, not_2_out, C, not_4_out);
  and and_12 (out_7, MSB, not_2_out, C, D);
  and and_13 (out_8, MSB, B, not_3_out, not_4_out);
  not not_4 (not_4_out, D);
  and and_14 (D13, MSB, B, not_3_out, D);
  and and_15 (D15, MSB, B, C, D);
  and and_16 (out_10, MSB, B, C, not_4_out);

  // Notes on the sheet:
  //   A
  //   D0
  //   D1
  //   D2
  //   D4
  //   D5
  //   D6
  //   D7
  //   D8
  //   D10
  //   (LSB)
  //   D11
  //   D12
  //   D14
endmodule
