// Logisim project Encoder.circ as structural Verilog: 1 circuit, main circuit main
module main (
  input  D0,
  input  D1,
  input  D2,
  input  D3,
  input  D4,
  input  D5,
  input  D6,
  input  D7,
  input  D8,
  input  D9,
  input  in_11,
  input  D11_prime_prime,
  input  D12,
  input  D13,
  input  D14,
  input  D15,
  output out_17,
  output B,
  output C,
  output D
);

  or or_1 (out_17, D8, D9, in_11, D11_prime_prime, D12, D13, D13, D15);
  or or_2 (B, D4, D5, D6, D7, D12, D13, D13, D15);
  or or_3 (C, D2, D3, D6, D7, in_11, D11_prime_prime, D13, D15);
  or or_4 (D, D1, D3, D5, D7, D9, D11_prime_prime, D13, D15);

  assign D14 = D13;

  // Notes on the sheet:
  //   D10
  //   16:4  ENCODER LOGISIM CIRCUIT
  //   A
endmodule
