// Logisim project half-adder.circ as structural Verilog: 1 circuit, main circuit main
module main (
  input  A,
  input  B,
  output out_3,
  output CARRY
);

  xor xor_1 (out_3, A, B);
  and and_1 (CARRY, A, B);

  // Notes on the sheet:
  //   (MSB)
  //   (LSB)
  //   SUM
endmodule
