// Logisim project full-adder.circ as structural Verilog: 2 circuits, main circuit main
module main (
  input  A_MSB,
  input  B,
  input  CIN,
  output SUM,
  output out_5
);

  wire half_adder_1_carry, half_adder_1_out_3, half_adder_2_carry;

  half_adder half_adder_1 (.A(A_MSB), .B(B), .out_3(half_adder_1_out_3), .CARRY(half_adder_1_carry));
  half_adder half_adder_2 (.A(half_adder_1_out_3), .B(CIN), .out_3(SUM), .CARRY(half_adder_2_carry));
  or or_1 (out_5, half_adder_2_carry, half_adder_1_carry);

  // Notes on the sheet:
  //   (LSB)
  //   CARRY
endmodule

module half_adder (
  input  A,
  input  B,
  output out_3,
  output CARRY
);

  xor xor_1 (out_3, A, B);
  and and_1 (CARRY, A, B);

  // Notes on the sheet:
  //   (MSB)
  //   (LSB)
  //   SUM
endmodule
