// Logisim project n-bit-adder-substractor.circ as structural Verilog: 3 circuits, main circuit main
module main (
  input  B1,
  input  A1,
  input  B0,
  input  in_4,
  input  A3,
  input  B2,
  input  A2,
  input  B3,
  input  M,
  output C,
  output V,
  output S2,
  output S3,
  output S1,
  output S0
);

  wire full_adder_2_out_5, full_adder_3_out_5, full_adder_4_out_5, xor_2_out, xor_3_out, xor_4_out, xor_5_out;

  xor xor_1 (V, C, full_adder_2_out_5);
  xor xor_2 (xor_2_out, B3, M);
  full_adder full_adder_1 (.A(A3), .B_prime(xor_2_out), .C(full_adder_2_out_5), .SUM(S3), .out_5(C));
  xor xor_3 (xor_3_out, B2, M);
  full_adder full_adder_2 (.A(A2), .B_prime(xor_3_out), .C(full_adder_3_out_5), .SUM(S2), .out_5(full_adder_2_out_5));
  full_adder full_adder_3 (.A(A1), .B_prime(xor_4_out), .C(full_adder_4_out_5), .SUM(S1), .out_5(full_adder_3_out_5));
  xor xor_4 (xor_4_out, B1, M);
  xor xor_5 (xor_5_out, B0, M);
  full_adder full_adder_4 (.A(in_4), .B_prime(xor_5_out), .C(M), .SUM(S0), .out_5(full_adder_4_out_5));

  // Notes on the sheet:
  //   FA
  //   (N=4)BIT ADDER/SUBSTRACTOR
  //   FA
  //   FA
  //   A0
  //   FA
endmodule

module full_adder (
  input  A,
  input  B_prime,
  input  C,
  output SUM,
  output out_5
);

  wire half_adder_1_carry, half_adder_1_out_3, half_adder_2_carry;

  half_adder half_adder_1 (.A(A), .B(B_prime), .out_3(half_adder_1_out_3), .CARRY(half_adder_1_carry));
  half_adder half_adder_2 (.A(half_adder_1_out_3), .B(C), .out_3(SUM), .CARRY(half_adder_2_carry));
  or or_1 (out_5, half_adder_2_carry, half_adder_1_carry);

  // Notes on the sheet:
  //   A(MSB)
  //   B
  //   CIN
  //   (LSB)
  //   CARRY
endmodule

module half_adder (
  input  A,
  input  B,
  output out_3,
  output CARRY
);

  xor xor_1 (out_3, A, B);
  and and_1 (CARRY, A, B);

  // Notes on the sheet:
  //   A
  //   B
  //   SUM
endmodule
